// Logisim project scott.circ as structural Verilog
module Main (
  input  [3:0] in_1,
  input  MANUAL,
  input  in_3
);

  wire and_1_out, CLOCK_out, cpu_1_halt, cpu_1_io_data_addr, cpu_1_r_w, cpu_1_ram_en, HALT_q, HALT_qn,
       led8_1__0, led8_1__1, led8_1__2, led8_1__3, led8_1__4, led8_1__5, led8_1__6, led8_1__7, led8_2__0,
       led8_2__1, led8_2__2, led8_2__3, led8_2__4, led8_2__5, led8_2__6, led8_2__7, led8_3__0, led8_3__1,
       led8_3__2, led8_3__3, led8_3__4, led8_3__5, led8_3__6, led8_3__7, led8_4__0, led8_4__1, led8_4__2,
       led8_4__3, led8_4__4, led8_4__5, led8_4__6, led8_4__7, led8_5__0, led8_5__1, led8_5__2, led8_5__3,
       led8_5__4, led8_5__5, led8_5__6, led8_5__7, led8_6__0, led8_6__1, led8_6__2, led8_6__3, led8_6__4,
       led8_6__5, led8_6__6, led8_6__7, led8_7__0, led8_7__1, led8_7__2, led8_7__3, led8_7__4, led8_7__5,
       led8_7__6, led8_7__7, led8_8__0, led8_8__1, led8_8__2, led8_8__3, led8_8__4, led8_8__5, led8_8__6,
       led8_8__7, led8_9__0, led8_9__1, led8_9__2, led8_9__3, led8_9__4, led8_9__5, led8_9__6, led8_9__7,
       led8_10__0, led8_10__1, led8_10__2, led8_10__3, led8_10__4, led8_10__5, led8_10__6, led8_10__7,
       led8_11__0, led8_11__1, led8_11__2, led8_11__3, led8_11__4, led8_11__5, led8_11__6, led8_11__7,
       led8_12__0, led8_12__1, led8_12__2, led8_12__3, led8_12__4, led8_12__5, led8_12__6, led8_12__7,
       led8_13__0, led8_13__1, led8_13__2, led8_13__3, led8_13__4, led8_13__5, led8_13__6, led8_13__7,
       led8_14__0, led8_14__1, led8_14__2, led8_14__3, led8_14__4, led8_14__5, led8_14__6, led8_14__7,
       led10_1__0, led10_1__1, led10_1__2, led10_1__3, led10_1__4, led10_1__5, led10_1__6, led10_1__7,
       led10_1__8, led10_1__9, multiplexer_1_out, n7segdisplay_1_a, n7segdisplay_1_b, n7segdisplay_1_c,
       n7segdisplay_1_d, n7segdisplay_1_dp, n7segdisplay_1_e, n7segdisplay_1_f, n7segdisplay_1_g, not_1_out,
       not_2_out, not_3_out, not_4_out, or_1_out, RESET_out, RESUME_out, STEP_out;
  wire [7:0] cpu2_1_dbga, cpu2_1_dbgb, cpu2_1_dbgd, cpu2_1_dbgfr, cpu2_1_dbgin, cpu2_1_dbgir, cpu2_1_dbgnpc,
       cpu2_1_dbgout, cpu2_1_dbgpc, cpu2_1_dbgr0, cpu2_1_dbgr1, cpu2_1_dbgr2, cpu2_1_dbgr3, cpu2_1_dbgsp,
       cpu_1_bus_out, cpu_1_ram_addr, cpu_1_rom_addr, INSTR_q, ram_1_data, rom_1_data;
  wire [9:0] cpu2_1_dbgaddr;

  Button RESET (.out(RESET_out));
  Button RESUME (.out(RESUME_out));
  not not_1 (not_1_out, MANUAL);
  Button STEP (.out(STEP_out));
  Clock CLOCK (.out(CLOCK_out));
  _7_Segment_Display u_7_segment_display_1 (
    .g(n7segdisplay_1_g), .f(n7segdisplay_1_f), .a(n7segdisplay_1_a), .b(n7segdisplay_1_b),
    .e(n7segdisplay_1_e), .d(n7segdisplay_1_d), .c(n7segdisplay_1_c), .dp(n7segdisplay_1_dp));
  _7SegDisplay u_7segdisplay_1 (
    .BCD_0(in_1), .a(n7segdisplay_1_a), .b(n7segdisplay_1_b), .c(n7segdisplay_1_c), .d(n7segdisplay_1_d),
    .e(n7segdisplay_1_e), .f(n7segdisplay_1_f), .dp(n7segdisplay_1_dp), .g(n7segdisplay_1_g));
  D_Flip_Flop HALT (
    .clk(cpu_1_halt), .D(HALT_qn), .Q(HALT_q), .Qn(HALT_qn), .en(1'b1), .reset(or_1_out));  // open: preset
  or or_1 (or_1_out, RESUME_out, RESET_out);
  Multiplexer #(.enable("false")) multiplexer_1 (
    .in0(STEP_out), .in1(CLOCK_out), .out(multiplexer_1_out), .sel(not_1_out));
  ROM rom_1 (.addr(cpu_1_rom_addr), .data(rom_1_data), .sel(1'b1));
  and and_1 (and_1_out, ~HALT_q, multiplexer_1_out);  // AND_Gate
  LED Reset_2 (.in(RESET_out));
  Counter INSTR (.load(1'b0), .count(1'b1), .Q(INSTR_q), .clk(not_2_out), .clr(RESET_out));  // open: D, carry
  not not_2 (not_2_out, and_1_out);
  Hex_Digit_Display hex_digit_display_1 (.value(INSTR_q[7:4]));  // open: dp
  LED Auto (.in(not_1_out));
  LED u_Manual (.in(MANUAL));
  _7_Segment_Display u_7_segment_display_2 ();  // open: g, f, a, b, e, d, c, dp
  CPU cpu_1 (
    .halt(cpu_1_halt), .clk(and_1_out), .rst(RESET_out), .r_w(cpu_1_r_w), .io_data_addr(cpu_1_io_data_addr),
    .ram_en(cpu_1_ram_en), .io_en(and_1_out), .ram_addr(cpu_1_ram_addr), .bus_out(cpu_1_bus_out),
    .bus_in(ram_1_data), .rom_addr(cpu_1_rom_addr), .rom_in(rom_1_data));  // open: dbg_ir, dbg_r0, dbg_r1, dbg_r2, dbg_r3, dbg_npc, dbg_pc, dbg_fr
  Hex_Digit_Display hex_digit_display_2 (.value(INSTR_q[3:0]));  // open: dp
  LED Halt_2 (.in(HALT_q));
  LED Clock_2 (.in(multiplexer_1_out));
  _7_Segment_Display u_7_segment_display_3 ();  // open: g, f, a, b, e, d, c, dp
  _7_Segment_Display u_7_segment_display_4 ();  // open: g, f, a, b, e, d, c, dp
  _7_Segment_Display u_7_segment_display_5 (.g(in_3));  // open: f, a, b, e, d, c, dp
  not not_3 (not_3_out, cpu_1_r_w);
  not not_4 (not_4_out, and_1_out);
  RAM #(.bus("separate")) ram_1 (
    .addr(cpu_1_ram_addr), .din(cpu_1_bus_out), .data(ram_1_data), .str(cpu_1_r_w), .sel(cpu_1_ram_en),
    .clk(not_4_out), .ld(not_3_out), .clr(RESET_out));
  CPU2 cpu2_1 (
    .dbgR2(cpu2_1_dbgr2), .dbgR3(cpu2_1_dbgr3), .dbgFR(cpu2_1_dbgfr), .dbgSP(cpu2_1_dbgsp),
    .dbgNPC(cpu2_1_dbgnpc), .dbgPC(cpu2_1_dbgpc), .dbgIR(cpu2_1_dbgir), .dbgR0(cpu2_1_dbgr0),
    .dbgR1(cpu2_1_dbgr1), .dbgADDR(cpu2_1_dbgaddr), .dbgA(cpu2_1_dbga), .dbgB(cpu2_1_dbgb),
    .dbgD(cpu2_1_dbgd), .dbgIN(cpu2_1_dbgin), .dbgOUT(cpu2_1_dbgout));  // open: mux_ra, mux_rb, mux_rd_2, mux_rd, selRA, selRB, selRD, op, cin, fr_w, rd_w, sp_w, ix, clk, reset, sp_inc_dec, ix_w, npc_w, pc_w, mux_npc, ADDR, BUS_OUT, BUS_IN, bus_ld_str, bus_en, branch, mux_addr, bus_en_2, bus_ld_str_2, br_op, halt, resume, instr, cycles
  LED led_1 (.in(led8_1__5));
  LED led_2 (.in(led8_1__7));
  LED led_3 (.in(led8_1__6));
  LED led_4 (.in(led8_2__6));
  LED led_5 (.in(led8_2__7));
  LED led_6 (.in(led8_2__5));
  LED led_7 (.in(led8_3__5));
  LED led_8 (.in(led8_3__7));
  LED led_9 (.in(led8_3__6));
  LED led_10 (.in(led8_4__6));
  LED led_11 (.in(led8_4__7));
  LED led_12 (.in(led8_4__5));
  LED led_13 (.in(led8_5__7));
  LED led_14 (.in(led8_5__5));
  LED led_15 (.in(led8_5__6));
  LED8 led8_1 (
    .in(cpu2_1_dbgr0), ._7(led8_1__7), ._6(led8_1__6), ._5(led8_1__5), ._4(led8_1__4), ._3(led8_1__3),
    ._2(led8_1__2), ._1(led8_1__1), ._0(led8_1__0));
  LED led_16 (.in(led8_1__3));
  LED led_17 (.in(led8_1__1));
  LED led_18 (.in(led8_1__4));
  LED led_19 (.in(led8_1__2));
  LED8 led8_2 (
    .in(cpu2_1_dbgr1), ._7(led8_2__7), ._6(led8_2__6), ._5(led8_2__5), ._4(led8_2__4), ._3(led8_2__3),
    ._2(led8_2__2), ._1(led8_2__1), ._0(led8_2__0));
  LED led_20 (.in(led8_2__2));
  LED led_21 (.in(led8_2__1));
  LED led_22 (.in(led8_2__3));
  LED led_23 (.in(led8_2__4));
  LED8 led8_3 (
    .in(cpu2_1_dbgr2), ._7(led8_3__7), ._6(led8_3__6), ._5(led8_3__5), ._4(led8_3__4), ._3(led8_3__3),
    ._2(led8_3__2), ._1(led8_3__1), ._0(led8_3__0));
  LED led_24 (.in(led8_3__2));
  LED led_25 (.in(led8_3__3));
  LED led_26 (.in(led8_3__4));
  LED led_27 (.in(led8_3__1));
  LED8 led8_4 (
    .in(cpu2_1_dbgr3), ._7(led8_4__7), ._6(led8_4__6), ._5(led8_4__5), ._4(led8_4__4), ._3(led8_4__3),
    ._2(led8_4__2), ._1(led8_4__1), ._0(led8_4__0));
  LED led_28 (.in(led8_4__3));
  LED led_29 (.in(led8_4__1));
  LED led_30 (.in(led8_4__2));
  LED led_31 (.in(led8_4__4));
  LED8 led8_5 (
    .in(cpu2_1_dbgsp), ._7(led8_5__7), ._6(led8_5__6), ._5(led8_5__5), ._4(led8_5__4), ._3(led8_5__3),
    ._2(led8_5__2), ._1(led8_5__1), ._0(led8_5__0));
  LED led_32 (.in(led8_5__1));
  LED led_33 (.in(led8_5__2));
  LED led_34 (.in(led8_5__4));
  LED led_35 (.in(led8_5__3));
  LED led_36 (.in(led8_1__0));
  LED led_37 (.in(led8_2__0));
  LED led_38 (.in(led8_3__0));
  LED led_39 (.in(led8_4__0));
  LED led_40 (.in(led8_5__0));
  ROM rom_2 ();  // open: addr, data, sel
  LED led_41 (.in(led8_6__6));
  LED led_42 (.in(led8_6__5));
  LED led_43 (.in(led8_6__7));
  LED led_44 (.in(led8_6__4));
  LED led_45 (.in(led8_7__6));
  LED led_46 (.in(led8_7__7));
  LED led_47 (.in(led8_7__4));
  LED led_48 (.in(led8_7__5));
  LED led_49 (.in(led8_8__5));
  LED led_50 (.in(led8_8__6));
  LED led_51 (.in(led8_8__7));
  LED led_52 (.in(led8_8__4));
  LED led_53 (.in(led8_9__6));
  LED led_54 (.in(led8_9__5));
  LED led_55 (.in(led8_9__4));
  LED led_56 (.in(led8_9__7));
  LED8 led8_6 (
    .in(cpu2_1_dbgnpc), ._7(led8_6__7), ._6(led8_6__6), ._5(led8_6__5), ._4(led8_6__4), ._3(led8_6__3),
    ._2(led8_6__2), ._1(led8_6__1), ._0(led8_6__0));
  LED led_57 (.in(led8_6__3));
  LED led_58 (.in(led8_6__1));
  LED led_59 (.in(led8_6__2));
  LED8 led8_7 (
    .in(cpu2_1_dbgpc), ._7(led8_7__7), ._6(led8_7__6), ._5(led8_7__5), ._4(led8_7__4), ._3(led8_7__3),
    ._2(led8_7__2), ._1(led8_7__1), ._0(led8_7__0));
  LED led_60 (.in(led8_7__3));
  LED led_61 (.in(led8_7__2));
  LED led_62 (.in(led8_7__1));
  LED8 led8_8 (
    .in(cpu2_1_dbgir), ._7(led8_8__7), ._6(led8_8__6), ._5(led8_8__5), ._4(led8_8__4), ._3(led8_8__3),
    ._2(led8_8__2), ._1(led8_8__1), ._0(led8_8__0));
  LED led_63 (.in(led8_8__3));
  LED led_64 (.in(led8_8__1));
  LED led_65 (.in(led8_8__2));
  LED8 led8_9 (
    .in(cpu2_1_dbgfr), ._7(led8_9__7), ._6(led8_9__6), ._5(led8_9__5), ._4(led8_9__4), ._3(led8_9__3),
    ._2(led8_9__2), ._1(led8_9__1), ._0(led8_9__0));
  LED led_66 (.in(led8_9__1));
  LED led_67 (.in(led8_9__3));
  LED led_68 (.in(led8_9__2));
  ROM rom_3 ();  // open: addr, data, sel
  LED led_69 (.in(led8_6__0));
  LED led_70 (.in(led8_7__0));
  LED led_71 (.in(led8_8__0));
  LED led_72 (.in(led8_9__0));
  LED led_73 (.in(led8_10__6));
  LED led_74 (.in(led8_10__7));
  LED led_75 (.in(led8_11__7));
  LED led_76 (.in(led8_11__6));
  LED led_77 (.in(led8_12__7));
  LED led_78 (.in(led8_12__6));
  LED led_79 (.in(led10_1__7));
  LED led_80 (.in(led10_1__8));
  LED led_81 (.in(led10_1__9));
  LED led_82 (.in(led10_1__6));
  LED led_83 (.in(led8_13__6));
  LED led_84 (.in(led8_13__7));
  LED led_85 (.in(led8_14__7));
  LED led_86 (.in(led8_14__6));
  LED8 led8_10 (
    .in(cpu2_1_dbga), ._7(led8_10__7), ._6(led8_10__6), ._5(led8_10__5), ._4(led8_10__4), ._3(led8_10__3),
    ._2(led8_10__2), ._1(led8_10__1), ._0(led8_10__0));
  LED led_87 (.in(led8_10__5));
  LED led_88 (.in(led8_10__4));
  LED led_89 (.in(led8_10__3));
  LED8 led8_11 (
    .in(cpu2_1_dbgb), ._7(led8_11__7), ._6(led8_11__6), ._5(led8_11__5), ._4(led8_11__4), ._3(led8_11__3),
    ._2(led8_11__2), ._1(led8_11__1), ._0(led8_11__0));
  LED led_90 (.in(led8_11__4));
  LED led_91 (.in(led8_11__3));
  LED led_92 (.in(led8_11__5));
  LED8 led8_12 (
    .in(cpu2_1_dbgd), ._7(led8_12__7), ._6(led8_12__6), ._5(led8_12__5), ._4(led8_12__4), ._3(led8_12__3),
    ._2(led8_12__2), ._1(led8_12__1), ._0(led8_12__0));
  LED led_93 (.in(led8_12__4));
  LED led_94 (.in(led8_12__5));
  LED led_95 (.in(led8_12__3));
  LED10 led10_1 (
    .in(cpu2_1_dbgaddr), ._9(led10_1__9), ._8(led10_1__8), ._7(led10_1__7), ._6(led10_1__6), ._5(led10_1__5),
    ._4(led10_1__4), ._3(led10_1__3), ._2(led10_1__2), ._1(led10_1__1), ._0(led10_1__0));
  LED led_96 (.in(led10_1__4));
  LED led_97 (.in(led10_1__3));
  LED led_98 (.in(led10_1__5));
  LED8 led8_13 (
    .in(cpu2_1_dbgin), ._7(led8_13__7), ._6(led8_13__6), ._5(led8_13__5), ._4(led8_13__4), ._3(led8_13__3),
    ._2(led8_13__2), ._1(led8_13__1), ._0(led8_13__0));
  LED led_99 (.in(led8_13__3));
  LED led_100 (.in(led8_13__4));
  LED led_101 (.in(led8_13__5));
  LED8 led8_14 (
    .in(cpu2_1_dbgout), ._7(led8_14__7), ._6(led8_14__6), ._5(led8_14__5), ._4(led8_14__4), ._3(led8_14__3),
    ._2(led8_14__2), ._1(led8_14__1), ._0(led8_14__0));
  LED led_102 (.in(led8_14__5));
  LED led_103 (.in(led8_14__3));
  LED led_104 (.in(led8_14__4));
  LED led_105 (.in(led8_10__1));
  LED led_106 (.in(led8_10__0));
  LED led_107 (.in(led8_10__2));
  LED led_108 (.in(led8_11__1));
  LED led_109 (.in(led8_11__0));
  LED led_110 (.in(led8_11__2));
  LED led_111 (.in(led8_12__2));
  LED led_112 (.in(led8_12__1));
  LED led_113 (.in(led8_12__0));
  LED led_114 (.in(led10_1__0));
  LED led_115 (.in(led10_1__2));
  LED led_116 (.in(led10_1__1));
  LED led_117 (.in(led8_13__2));
  LED led_118 (.in(led8_13__0));
  LED led_119 (.in(led8_13__1));
  LED led_120 (.in(led8_14__0));
  LED led_121 (.in(led8_14__2));
  LED led_122 (.in(led8_14__1));
  ROM rom_4 ();  // open: addr, data, sel

  // Notes on the sheet:
  //   contents of rom_1 (hex, n*v repeats v):
  //   1c 5 14 1 9 10 2 fc 54 a 1 82 9 4 10 1 9c 50 f3 10 1 34 60
  //   0000 ra rb  ->  mov  ra, rb    ->  ra = rb
  //   0001 ra xx  ->  data ra, imm8  ->  ra = ram[pc++]
  //   0010 ra rb  ->  ldr  ra, [rb]  ->  ra = ram[rb]
  //   0011 ra rb  ->  str  ra, [rb]  ->  ram[rb] = ra
  //   0100 ra ra  ->  jalr ra        ->  pc <-> ra
  //   0101  cond  ->  b<cond> imm8   ->  pc += cond ? ram[pc] : 1
  //   0110 00 00  ->  halt           ->  stop computer
  //   0111 ra 00  ->  in   ra, data  ->  ra = io[active].data
  //   0111 ra 10  ->  out  ra, data  ->  io[active].data = ra
  //   0111 ra 01  ->  in   ra, addr  ->  ra = io[active].addr
  //   0111 ra 11  ->  out  ra, addr  ->  io[ra].active = true
  //   1000 ra rb  ->  add  ra, rb    ->  ra = ra + rb       [vcsz]
  //   1001 ra rb  ->  sub  ra, rb    ->  ra = ra - rb       [vcsz]
  //   1010 ra rb  ->  shl  ra, rb    ->  ra = [rb << 1, 0]  [0csz]
  //   1011 ra rb  ->  shr  ra, rb    ->  ra = [0, rb >> 1]  [0csz]
  //   1100 ra rb  ->  and  ra, rb    ->  ra = ra & rb       [00sz]
  //   1101 ra rb  ->  orr  ra, rb    ->  ra = ra | rb       [00sz]
  //   1110 ra rb  ->  xor  ra, rb    ->  ra = ra ^ rb       [00sz]
  //   1111 ra rb  ->  cmp  ra, rb    ->  fr = ra - rb       [vcsz]
  //   bits | cond   | flag test  | description
  //   0000 | r      | -----      | branch always
  //   0001 | zs/eq  | z=1        | branch if equal
  //   0010 | ss/neg | s=1        | branch if negative
  //   0011 | ov     | v=1        | branch if overflow
  //   0100 | cs/ltu | c=1        | branch if uint <
  //   0101 | leu    | c=1 or z=1 | branch if uint <=
  //   0110 | lt     | v+s        | branch if int <
  //   0111 | le     | v+s or z=1 | branch if int <=
  //   contents of rom_2 (hex, n*v repeats v):
  //   1c 5 14 1 9 10 2 fc 54 a 1 82 9 4 10 1 9c 50 f3 10 1 34 60
  //   contents of rom_3 (hex, n*v repeats v):
  //   1c 5 14 1 9 10 2 fc 54 a 1 82 9 4 10 1 9c 50 f3 10 1 34 60
  //   contents of rom_4 (hex, n*v repeats v):
  //   1c 5 14 1 9 10 2 fc 54 a 1 82 9 4 10 1 9c 50 f3 10 1 34 60
endmodule

module CPU (
  input  [7:0] bus_in,
  input  clk,
  input  rst,
  input  [7:0] rom_in,
  output [7:0] dbg_ir,
  output io_data_addr,
  output r_w,
  output ram_en,
  output io_en,
  output [7:0] dbg_r0,
  output halt,
  output [3:0] dbg_fr,
  output [7:0] dbg_r1,
  output [7:0] dbg_r2,
  output [7:0] dbg_r3,
  output [7:0] dbg_npc,
  output [7:0] dbg_pc,
  output [7:0] ram_addr,
  output [7:0] bus_out,
  output [7:0] rom_addr
);

  wire and_2_out, and_3_out, and_4_out, and_5_out, and_6_out, branchchecker_1_result, d_ff_1_q, d_ff_1_qn,
       not_1_out, not_2_out, not_3_out, or_1_out, or_2_out, or_4_out;
  wire [3:0] reg4_1_out_3__0, undriven;
  wire [7:0] alu_1_p11, controlled_buffer_1_out, inc8_1_p1, multiplexer_1_out, multiplexer_3_out,
       multiplexer_4_out, multiplexer_5_out, multiplexer_6_out, reg8_1_out, regfile_1_ra, regfile_1_rb;
  wire [15:0] rom_1_data;

  and and_1 (halt, rom_1_data[15], not_1_out);
  not not_1 (not_1_out, clk);
  and and_2 (and_2_out, rom_1_data[13], branchchecker_1_result, d_ff_1_q);
  or or_1 (or_1_out, rom_1_data[12], and_2_out);
  Multiplexer #(.width(8), .enable("false")) multiplexer_1 (
    .in0(inc8_1_p1), .in1(alu_1_p11), .out(multiplexer_1_out), .sel(or_1_out));
  BranchChecker branchchecker_1 (
    .zero(undriven[0]), .sign(undriven[1]), .carry(undriven[2]), .overflow(undriven[3]),
    .result(branchchecker_1_result));  // open: op0, op1, op2
  Reg8 reg8_1 (
    .in(multiplexer_1_out), .dbg(dbg_npc), .r(1'b1), .w(1'b1), .en(1'b1), .clk(not_1_out), .rst(rst),
    .out(reg8_1_out));
  // Inc8 inc8_1: pin names not known; wires that end beside it: inc8_1_p1, 1'b1, 1'b0, rom_addr
  Reg8 reg8_2 (
    .in(reg8_1_out), .dbg(dbg_pc), .r(1'b1), .w(1'b1), .en(1'b1), .clk(not_2_out), .rst(rst), .out(rom_addr));
  not not_2 (not_2_out, not_1_out);
  and and_3 (and_3_out, rom_1_data[14], not_1_out);
  D_Flip_Flop d_ff_1 (
    .clk(and_3_out), .D(d_ff_1_qn), .Q(d_ff_1_q), .Qn(d_ff_1_qn), .en(1'b1), .reset(rst));  // open: preset
  Multiplexer #(.width(8), .enable("false")) multiplexer_2 (.in0(rom_in), .in1(dbg_ir), .out(dbg_ir), .sel(d_ff_1_q));
  ROM #(.addrWidth(4), .dataWidth(16)) rom_1 (
    .addr(dbg_ir[7:4]), .data({rom_1_data[15:12], io_en, ram_en, rom_1_data[9:0]}), .sel(1'b1));
  RegFile regfile_1 (
    .rd(multiplexer_3_out), .reg_w(or_2_out), .selRD0(dbg_ir[2]), .selRD1(dbg_ir[3]), .clk(not_1_out),
    .rst(rst), .selRA0(dbg_ir[2]), .selRA1(dbg_ir[3]), .selRB0(dbg_ir[0]), .selRB1(dbg_ir[1]),
    .ra(regfile_1_ra), .rb(regfile_1_rb), .dbgR3(dbg_r0), .dbgR2(dbg_r1), .dbgR0(dbg_r3), .dbgR1(dbg_r2));
  or or_2 (or_2_out, and_4_out, rom_1_data[8]);
  and and_4 (and_4_out, dbg_ir[1], io_en);
  Multiplexer #(.width(8), .enable("false")) multiplexer_3 (
    .in0(alu_1_p11), .in1(multiplexer_4_out), .out(multiplexer_3_out), .sel(rom_1_data[6]));
  Multiplexer #(.width(8), .enable("false")) multiplexer_4 (
    .in0(inc8_1_p1), .in1(controlled_buffer_1_out), .out(multiplexer_4_out), .sel(rom_1_data[7]));
  Multiplexer #(.width(8), .enable("false")) multiplexer_5 (
    .in0(regfile_1_ra), .in1(rom_addr), .out(multiplexer_5_out), .sel(rom_1_data[5]));
  Multiplexer #(.width(8), .enable("false")) multiplexer_6 (
    .in0(regfile_1_rb), .in1(rom_in), .out(multiplexer_6_out), .sel(rom_1_data[4]));
  Reg4 reg4_1 (
    .r(1'b1), .w(rom_1_data[2]), .en(1'b1), .clk(not_1_out), .rst(rst), .in_3__0(undriven),
    .out_3__0(reg4_1_out_3__0), .dbg_3__0(dbg_fr));
  // ALU_2 alu_1: pin names not known; wires that end beside it: multiplexer_5_out, multiplexer_6_out, reg4_1_out_3__0[3], reg4_1_out_3__0[2], reg4_1_out_3__0[1], reg4_1_out_3__0[0], 1'b0, rom_1_data[2], rom_1_data[1], rom_1_data[0], alu_1_p11
  assign controlled_buffer_1_out = and_6_out ? bus_in : 8'bz;  // Controlled_Buffer controlled_buffer_1
  or or_3 (r_w, dbg_ir[1], rom_1_data[9]);
  or or_4 (or_4_out, io_en, ram_en);
  Multiplexer #(.width(8), .disabled(0), .enable("false")) multiplexer_7 (
    .in0(ram_addr), .in1(alu_1_p11), .out(ram_addr), .sel(ram_en));
  Pull_Resistor pull_resistor_1 (.node(ram_addr));
  assign bus_out = and_5_out ? regfile_1_ra : 8'bz;  // Controlled_Buffer controlled_buffer_2
  and and_5 (and_5_out, or_4_out, r_w);
  and and_6 (and_6_out, or_4_out, not_3_out);
  not not_3 (not_3_out, r_w);

  assign io_data_addr = dbg_ir[0];

  // Notes on the sheet:
  //   contents of rom_1 (hex, n*v repeats v):
  //   100 4110 5c0 6c0 1180 6034 8000 8c0 10c 10d 10e 10f 109 10a 10b d
endmodule

module CPU2 (
  input  mux_npc,
  input  mux_ra,
  input  [2:0] op,
  input  mux_rd,
  input  [1:0] ix,
  input  fr_w,
  input  sp_w,
  input  cin,
  input  sp_inc_dec,
  input  halt,
  input  bus_ld_str,
  input  mux_rb,
  input  branch,
  input  [1:0] selRA,
  input  mux_rd_2,
  input  npc_w,
  input  [2:0] br_op,
  input  [1:0] selRB,
  input  ix_w,
  input  bus_en,
  input  [1:0] mux_addr,
  input  [1:0] selRD,
  input  pc_w,
  input  rd_w,
  input  clk,
  input  reset,
  input  resume,
  input  [7:0] BUS_IN,
  output [7:0] dbgR0,
  output [7:0] instr,
  output [7:0] dbgR1,
  output [7:0] dbgR2,
  output [7:0] dbgR3,
  output [7:0] dbgSP,
  output [7:0] dbgNPC,
  output [7:0] dbgPC,
  output [7:0] dbgIR,
  output [7:0] dbgFR,
  output [7:0] dbgA,
  output [7:0] dbgB,
  output [7:0] dbgD,
  output [7:0] dbgIN,
  output [7:0] dbgOUT,
  output [9:0] dbgADDR,
  output [12:0] cycles,
  output bus_en_2,
  output bus_ld_str_2,
  output [9:0] ADDR,
  output [7:0] BUS_OUT
);

  wire and_1_out, and_2_out, and_3_out, and_4_out, and_5_out, and_6_out, branchchecker_1_result, halt_qn,
       ifetch_exec_q, ifetch_exec_qn, nand_1_out, not_1_out, not_2_out, or_1_out, or_2_out, or_3_out,
       or_4_out;
  wire [3:0] alu_1_zero, reg4_1_out_3__0;
  wire [7:0] alu_1_out, inc8_1_out, inc8_2_out, multiplexer_1_out, reg8_2_out, reg8_3_out, reg8_4_out,
       regfile_1_rb;

  nand nand_1 (nand_1_out, clk, halt_qn);
  not not_1 (not_1_out, reset);
  T_Flip_Flop ifetch_exec (
    .clk(nand_1_out), .T(1'b1), .Q(ifetch_exec_q), .Qn(ifetch_exec_qn), .reset(not_1_out), .en(1'b1));  // open: preset
  T_Flip_Flop u_halt (
    .clk(nand_1_out), .T(halt_qn), .Q(dbgFR[7]), .Qn(halt_qn), .reset(or_1_out), .en(and_1_out));  // open: preset
  and and_1 (and_1_out, halt, ifetch_exec_q);
  or or_1 (or_1_out, not_1_out, resume);
  Reg8 reg8_1 (
    .in(BUS_IN), .dbg(dbgIR), .r(1'b1), .w(ifetch_exec_qn), .en(1'b1), .clk(nand_1_out), .rst(not_1_out),
    .out(instr));
  Counter #(.width(13), .max('h1fff)) u_cycles (
    .count(1'b1), .Q(cycles), .clk(ifetch_exec_qn), .clr(not_1_out));  // open: load, D, carry
  or or_2 (or_2_out, mux_npc, and_2_out);
  and and_2 (and_2_out, branch, branchchecker_1_result);
  Multiplexer #(.width(8), .enable("false")) multiplexer_1 (
    .in0(inc8_1_out), .in1(alu_1_out), .out(multiplexer_1_out), .sel(or_2_out));
  or or_3 (or_3_out, npc_w, ifetch_exec_qn);
  BranchChecker branchchecker_1 (
    .zero(reg4_1_out_3__0[0]), .sign(reg4_1_out_3__0[1]), .carry(reg4_1_out_3__0[2]),
    .overflow(reg4_1_out_3__0[3]), .op0(br_op[0]), .op1(br_op[1]), .op2(br_op[2]),
    .result(branchchecker_1_result));
  Reg8 reg8_2 (
    .in(multiplexer_1_out), .dbg(dbgNPC), .r(1'b1), .w(or_3_out), .en(1'b1), .clk(nand_1_out),
    .rst(not_1_out), .out(reg8_2_out));
  Multiplexer #(.select(2), .width(10), .enable("false")) multiplexer_2 (
    .in0({2'b00, reg8_3_out}), .in1({dbgFR[5:4], alu_1_out}), .in2({2'b01, reg8_4_out}),
    .in3({2'b01, inc8_2_out}), .out(ADDR), .sel(mux_addr));
  Reg8 reg8_3 (
    .in(reg8_2_out), .dbg(dbgPC), .r(1'b1), .w(or_4_out), .en(1'b1), .clk(not_2_out), .rst(not_1_out),
    .out(reg8_3_out));
  not not_2 (not_2_out, nand_1_out);
  or or_4 (or_4_out, pc_w, ifetch_exec_qn);
  Inc8 inc8_1 (.in(reg8_3_out), .out(inc8_1_out), .cin(1'b1), .add_sub(1'b0));  // open: cout
  and and_3 (and_3_out, rd_w, ifetch_exec_q);
  RegFile regfile_1 (
    .rd(dbgD), .reg_w(and_3_out), .selRD0(selRD[0]), .selRD1(selRD[1]), .clk(nand_1_out), .rst(not_1_out),
    .selRA0(selRA[0]), .selRA1(selRA[1]), .selRB0(selRB[0]), .selRB1(selRB[1]), .ra(BUS_OUT),
    .rb(regfile_1_rb), .dbgR3(dbgR3), .dbgR2(dbgR2), .dbgR0(dbgR0), .dbgR1(dbgR1));
  RegMux regmux_1 (
    .RAin0(BUS_OUT), .RAin1(reg8_3_out), .RBin0(regfile_1_rb), .RBin1(BUS_IN), .RDout(dbgD), .RAout(dbgA),
    .RBout(dbgB), .RDin0(alu_1_out), .RDin1(BUS_IN), .RDin2(inc8_1_out), .muxRA(mux_ra), .muxRB(mux_rb),
    .muxRD1(mux_rd_2), .muxRD0(mux_rd));
  and and_4 (and_4_out, ix_w, nand_1_out);
  D_Flip_Flop d_ff_1 (.clk(and_4_out), .D(ix[0]), .Q(dbgFR[4]), .en(1'b1), .reset(not_1_out));  // open: Qn, preset
  D_Flip_Flop d_ff_2 (.clk(and_4_out), .D(ix[1]), .Q(dbgFR[5]), .preset(not_1_out), .en(1'b1));  // open: Qn, reset
  Reg4 reg4_1 (
    .r(1'b1), .w(and_5_out), .en(1'b1), .clk(nand_1_out), .rst(not_1_out), .in_3__0(alu_1_zero),
    .out_3__0(reg4_1_out_3__0), .dbg_3__0(dbgFR[3:0]));
  and and_5 (and_5_out, ifetch_exec_q, fr_w);
  ALU_2 alu_1 (
    .cin(cin), .op2(op[2]), .op1(op[1]), .op0(op[0]), .overflow(alu_1_zero[3]), .sign(alu_1_zero[1]),
    .zero(alu_1_zero[0]), .carry(alu_1_zero[2]), .out(alu_1_out), .b(dbgB), .a(dbgA));
  and and_6 (and_6_out, sp_w, ifetch_exec_q);
  Inc8 inc8_2 (.in(reg8_4_out), .out(inc8_2_out), .cin(1'b1), .add_sub(sp_inc_dec));  // open: cout
  Reg8 reg8_4 (
    .in(inc8_2_out), .dbg(dbgSP), .r(1'b1), .w(and_6_out), .en(1'b1), .clk(nand_1_out), .rst(not_1_out),
    .out(reg8_4_out));

  assign bus_en_2 = bus_en;
  assign bus_ld_str_2 = bus_ld_str;
  assign dbgADDR = ADDR;
  assign dbgIN = BUS_IN;
  assign dbgOUT = BUS_OUT;

  // Other names for the same wires on the sheet: IX_t[1:0] = dbgFR[5:4]; A[7:0] = dbgA; B[7:0] = dbgB; D[7:0] = dbgD;
  //   FR[3:0] = dbgFR[3:0]; MAN = dbgFR[6]; HALT_t = dbgFR[7]; IN[7:0] = BUS_IN; IR[7:0] = dbgIR; NPC[7:0] = dbgNPC;
  //   OUT[7:0] = BUS_OUT; PC[7:0] = dbgPC; R0[7:0] = dbgR0; R1[7:0] = dbgR1; R2[7:0] = dbgR2; R3[7:0] = dbgR3;
  //   SP[7:0] = dbgSP
endmodule

module LED8 (
  input  [7:0] in,
  output _7,
  output _6,
  output _5,
  output _4,
  output _3,
  output _2,
  output _1,
  output _0
);


  assign _0 = in[0];
  assign _1 = in[1];
  assign _2 = in[2];
  assign _3 = in[3];
  assign _4 = in[4];
  assign _5 = in[5];
  assign _6 = in[6];
  assign _7 = in[7];
endmodule

module LED10 (
  input  [9:0] in,
  output _9,
  output _8,
  output _7,
  output _6,
  output _5,
  output _4,
  output _3,
  output _2,
  output _1,
  output _0
);


  assign _0 = in[0];
  assign _1 = in[1];
  assign _2 = in[2];
  assign _3 = in[3];
  assign _4 = in[4];
  assign _5 = in[5];
  assign _6 = in[6];
  assign _7 = in[7];
  assign _8 = in[8];
  assign _9 = in[9];
endmodule

module _7SegDisplay (
  input  [3:0] BCD_0,
  output a,
  output b,
  output c,
  output d,
  output e,
  output f,
  output g,
  output dp
);

  wire decoder_1_out0, decoder_1_out1, decoder_1_out2, decoder_1_out3, decoder_1_out4, decoder_1_out5,
       decoder_1_out6, decoder_1_out7, decoder_1_out8, decoder_1_out9;

  Decoder #(.select(4), .enable("false")) decoder_1 (
    .out0(decoder_1_out0), .out1(decoder_1_out1), .out2(decoder_1_out2), .out3(decoder_1_out3),
    .out4(decoder_1_out4), .out5(decoder_1_out5), .out6(decoder_1_out6), .out7(decoder_1_out7),
    .out8(decoder_1_out8), .out9(decoder_1_out9), .sel(BCD_0));  // open: out10, out11, out12, out13, out14, out15
  or or_1 (a, decoder_1_out9, decoder_1_out8, decoder_1_out7, decoder_1_out6, decoder_1_out5, 1'b0, decoder_1_out3, decoder_1_out2, 1'b0, decoder_1_out0);
  or or_2 (b, decoder_1_out9, decoder_1_out8, decoder_1_out7, 1'b0, 1'b0, decoder_1_out4, decoder_1_out3, decoder_1_out2, decoder_1_out1, decoder_1_out0);
  or or_3 (c, decoder_1_out9, decoder_1_out8, decoder_1_out7, decoder_1_out6, decoder_1_out5, decoder_1_out4, decoder_1_out3, 1'b0, decoder_1_out1, decoder_1_out0);
  or or_4 (d, decoder_1_out9, decoder_1_out8, 1'b0, decoder_1_out6, decoder_1_out5, 1'b0, decoder_1_out3, decoder_1_out2, 1'b0, decoder_1_out0);
  or or_5 (e, 1'b0, decoder_1_out8, 1'b0, decoder_1_out6, 1'b0, 1'b0, 1'b0, decoder_1_out2, 1'b0, decoder_1_out0);
  or or_6 (f, decoder_1_out9, decoder_1_out8, 1'b0, decoder_1_out6, decoder_1_out5, decoder_1_out4, 1'b0, 1'b0, 1'b0, decoder_1_out0);
  or or_7 (g, decoder_1_out9, decoder_1_out8, 1'b0, decoder_1_out6, decoder_1_out5, decoder_1_out4, decoder_1_out3, decoder_1_out2, 1'b0, 1'b0);
  or or_8 (dp, 1'b0, 1'b0, 1'b0, 1'b0, 1'b0, 1'b0, 1'b0, 1'b0, 1'b0, 1'b0);
endmodule

module MemoryUnit (
  input  ld,
  input  str,
  output [9:0] addr,
  output [7:0] data_in,
  output [7:0] data_out
);

  wire decoder_1_out0, decoder_1_out1, decoder_1_out2, decoder_1_out3;
  wire [7:0] controlled_buffer_1_out, controlled_buffer_2_out, controlled_buffer_3_out, demultiplexer_1_out0,
       demultiplexer_1_out1, demultiplexer_1_out2, demultiplexer_1_out3, demultiplexer_2_out1,
       demultiplexer_2_out2, demultiplexer_2_out3, ram_1_data, ram_2_data, ram_3_data, rom_1_data;

  Decoder #(.select(2), .enable("false")) decoder_1 (
    .out0(decoder_1_out0), .out1(decoder_1_out1), .out2(decoder_1_out2), .out3(decoder_1_out3),
    .sel(addr[9:8]));
  Demultiplexer #(.select(2), .width(8), .enable("false")) demultiplexer_1 (
    .out0(demultiplexer_1_out0), .out1(demultiplexer_1_out1), .out2(demultiplexer_1_out2),
    .out3(demultiplexer_1_out3), .in(addr[7:0]), .sel(addr[9:8]));
  ROM rom_1 (.addr(demultiplexer_1_out0), .data(rom_1_data), .sel(decoder_1_out0));
  RAM ram_1 (.addr(demultiplexer_1_out1), .data(ram_1_data), .sel(decoder_1_out1));  // open: clk, ld, clr
  RAM ram_2 (.addr(demultiplexer_1_out2), .data(ram_2_data), .sel(decoder_1_out2));  // open: clk, ld, clr
  RAM ram_3 (.addr(demultiplexer_1_out3), .data(ram_3_data), .sel(decoder_1_out3));  // open: clk, ld, clr
  Multiplexer #(.select(2), .width(8), .enable("false")) multiplexer_1 (
    .in0(rom_1_data), .in1(controlled_buffer_1_out), .in2(controlled_buffer_2_out),
    .in3(controlled_buffer_3_out), .out(data_in), .sel(addr[9:8]));
  assign controlled_buffer_1_out = ld ? ram_1_data : 8'bz;  // Controlled_Buffer controlled_buffer_1
  assign controlled_buffer_2_out = ld ? ram_2_data : 8'bz;  // Controlled_Buffer controlled_buffer_2
  assign controlled_buffer_3_out = ld ? ram_3_data : 8'bz;  // Controlled_Buffer controlled_buffer_3
  assign ram_1_data = str ? demultiplexer_2_out1 : 8'bz;  // Controlled_Buffer controlled_buffer_4
  Demultiplexer #(.select(2), .width(8), .enable("false")) demultiplexer_2 (
    .out1(demultiplexer_2_out1), .out2(demultiplexer_2_out2), .out3(demultiplexer_2_out3), .in(data_out),
    .sel(addr[9:8]));  // open: out0
  assign ram_2_data = str ? demultiplexer_2_out2 : 8'bz;  // Controlled_Buffer controlled_buffer_5
  assign ram_3_data = str ? demultiplexer_2_out3 : 8'bz;  // Controlled_Buffer controlled_buffer_6

  // Notes on the sheet:
  //   IO
  //   ROM
  //   STACK
  //   RAM
endmodule

module RegFile (
  input  [7:0] rd,
  input  reg_w,
  input  selRD0,
  input  selRD1,
  input  clk,
  input  rst,
  input  selRA0,
  input  selRA1,
  input  selRB0,
  input  selRB1,
  output [7:0] dbgR0,
  output [7:0] dbgR1,
  output [7:0] dbgR2,
  output [7:0] dbgR3,
  output [7:0] ra,
  output [7:0] rb
);

  wire and_1_out, and_2_out, and_3_out, and_4_out, decoder_1_out0, decoder_1_out1, decoder_1_out2,
       decoder_1_out3;
  wire [7:0] reg8_1_out, reg8_2_out, reg8_3_out, reg8_4_out;

  Decoder #(.select(2), .enable("false")) decoder_1 (
    .out0(decoder_1_out0), .out1(decoder_1_out1), .out2(decoder_1_out2), .out3(decoder_1_out3),
    .sel({selRD1, selRD0}));
  and and_1 (and_1_out, reg_w, decoder_1_out0);
  Reg8 reg8_1 (.in(rd), .dbg(dbgR0), .r(1'b1), .w(and_1_out), .en(1'b1), .clk(clk), .rst(rst), .out(reg8_1_out));
  and and_2 (and_2_out, reg_w, decoder_1_out1);
  Reg8 reg8_2 (.in(rd), .dbg(dbgR1), .r(1'b1), .w(and_2_out), .en(1'b1), .clk(clk), .rst(rst), .out(reg8_2_out));
  Reg8 reg8_3 (.in(rd), .dbg(dbgR2), .r(1'b1), .w(and_3_out), .en(1'b1), .clk(clk), .rst(rst), .out(reg8_3_out));
  and and_3 (and_3_out, reg_w, decoder_1_out2);
  Reg8 reg8_4 (.in(rd), .dbg(dbgR3), .r(1'b1), .w(and_4_out), .en(1'b1), .clk(clk), .rst(rst), .out(reg8_4_out));
  and and_4 (and_4_out, reg_w, decoder_1_out3);
  Multiplexer #(.select(2), .width(8), .enable("false")) multiplexer_1 (
    .in0(reg8_4_out), .in1(reg8_3_out), .in2(reg8_2_out), .in3(reg8_1_out), .out(ra), .sel({selRA1, selRA0}));
  Multiplexer #(.select(2), .width(8), .enable("false")) multiplexer_2 (
    .in0(reg8_4_out), .in1(reg8_3_out), .in2(reg8_2_out), .in3(reg8_1_out), .out(rb), .sel({selRB1, selRB0}));
endmodule

module RegMux (
  input  muxRA,
  input  [7:0] RAin0,
  input  [7:0] RAin1,
  input  muxRB,
  input  [7:0] RBin0,
  input  [7:0] RBin1,
  input  muxRD1,
  input  muxRD0,
  input  [7:0] RDin0,
  input  [7:0] RDin1,
  input  [7:0] RDin2,
  output [7:0] RAout,
  output [7:0] RBout,
  output [7:0] RDout
);

  wire [7:0] multiplexer_3_out;

  Multiplexer #(.width(8), .enable("false")) multiplexer_1 (.in0(RAin0), .in1(RAin1), .out(RAout), .sel(muxRA));
  Multiplexer #(.width(8), .enable("false")) multiplexer_2 (.in0(RBin0), .in1(RBin1), .out(RBout), .sel(muxRB));
  Multiplexer #(.width(8), .enable("false")) multiplexer_3 (
    .in0(RDin0), .in1(RDin1), .out(multiplexer_3_out), .sel(muxRD0));
  Multiplexer #(.width(8), .enable("false")) multiplexer_4 (
    .in0(multiplexer_3_out), .in1(RDin2), .out(RDout), .sel(muxRD1));
endmodule

module Reg4 (
  input  [3:0] in_3__0,
  input  r,
  input  w,
  input  en,
  input  clk,
  input  rst,
  output [3:0] dbg_3__0,
  output [3:0] out_3__0
);

  wire and_1_out, and_2_out, and_3_out, and_4_out, multiplexer_1_out, multiplexer_2_out, multiplexer_3_out,
       multiplexer_4_out, nand_1_out, nand_2_out, nand_3_out, nand_4_out;

  Multiplexer #(.enable("false")) multiplexer_1 (
    .in0(in_3__0[3]), .in1(dbg_3__0[3]), .out(multiplexer_1_out), .sel(nand_1_out));
  nand nand_1 (nand_1_out, w, en);
  D_Flip_Flop d_ff_1 (
    .clk(clk), .D(multiplexer_1_out), .Q(dbg_3__0[3]), .preset(1'b0), .en(en), .reset(rst));  // open: Qn
  assign out_3__0[3] = and_1_out ? dbg_3__0[3] : 1'bz;  // Controlled_Buffer controlled_buffer_1
  nand nand_2 (nand_2_out, w, en);
  and and_1 (and_1_out, r, en);
  Multiplexer #(.enable("false")) multiplexer_2 (
    .in0(in_3__0[2]), .in1(dbg_3__0[2]), .out(multiplexer_2_out), .sel(nand_2_out));
  D_Flip_Flop d_ff_2 (
    .clk(clk), .D(multiplexer_2_out), .Q(dbg_3__0[2]), .preset(1'b0), .en(en), .reset(rst));  // open: Qn
  assign out_3__0[2] = and_2_out ? dbg_3__0[2] : 1'bz;  // Controlled_Buffer controlled_buffer_2
  nand nand_3 (nand_3_out, w, en);
  and and_2 (and_2_out, r, en);
  Multiplexer #(.enable("false")) multiplexer_3 (
    .in0(in_3__0[1]), .in1(dbg_3__0[1]), .out(multiplexer_3_out), .sel(nand_3_out));
  D_Flip_Flop d_ff_3 (
    .clk(clk), .D(multiplexer_3_out), .Q(dbg_3__0[1]), .preset(1'b0), .en(en), .reset(rst));  // open: Qn
  assign out_3__0[1] = and_3_out ? dbg_3__0[1] : 1'bz;  // Controlled_Buffer controlled_buffer_3
  and and_3 (and_3_out, r, en);
  Multiplexer #(.enable("false")) multiplexer_4 (
    .in0(in_3__0[0]), .in1(dbg_3__0[0]), .out(multiplexer_4_out), .sel(nand_4_out));
  nand nand_4 (nand_4_out, w, en);
  D_Flip_Flop d_ff_4 (
    .clk(clk), .D(multiplexer_4_out), .Q(dbg_3__0[0]), .preset(1'b0), .en(en), .reset(rst));  // open: Qn
  assign out_3__0[0] = and_4_out ? dbg_3__0[0] : 1'bz;  // Controlled_Buffer controlled_buffer_4
  and and_4 (and_4_out, r, en);
endmodule

module Reg8 (
  input  [7:0] in,
  input  r,
  input  w,
  input  en,
  input  clk,
  input  rst,
  output [7:0] dbg,
  output [7:0] out
);

  wire and_1_out, and_2_out, and_3_out, and_4_out, and_5_out, and_6_out, and_7_out, and_8_out,
       multiplexer_1_out, multiplexer_2_out, multiplexer_3_out, multiplexer_4_out, multiplexer_5_out,
       multiplexer_6_out, multiplexer_7_out, multiplexer_8_out, nand_1_out, nand_2_out, nand_3_out,
       nand_4_out, nand_5_out, nand_6_out, nand_7_out, nand_8_out;

  nand nand_1 (nand_1_out, w, en);
  Multiplexer #(.enable("false")) multiplexer_1 (.in0(in[7]), .in1(dbg[7]), .out(multiplexer_1_out), .sel(nand_1_out));
  D_Flip_Flop d_ff_1 (.clk(clk), .D(multiplexer_1_out), .Q(dbg[7]), .preset(1'b0), .en(en), .reset(rst));  // open: Qn
  assign out[7] = and_1_out ? dbg[7] : 1'bz;  // Controlled_Buffer controlled_buffer_1
  nand nand_2 (nand_2_out, w, en);
  and and_1 (and_1_out, r, en);
  Multiplexer #(.enable("false")) multiplexer_2 (.in0(in[6]), .in1(dbg[6]), .out(multiplexer_2_out), .sel(nand_2_out));
  D_Flip_Flop d_ff_2 (.clk(clk), .D(multiplexer_2_out), .Q(dbg[6]), .preset(1'b0), .en(en), .reset(rst));  // open: Qn
  assign out[6] = and_2_out ? dbg[6] : 1'bz;  // Controlled_Buffer controlled_buffer_2
  and and_2 (and_2_out, r, en);
  Multiplexer #(.enable("false")) multiplexer_3 (.in0(in[5]), .in1(dbg[5]), .out(multiplexer_3_out), .sel(nand_3_out));
  nand nand_3 (nand_3_out, w, en);
  D_Flip_Flop d_ff_3 (.clk(clk), .D(multiplexer_3_out), .Q(dbg[5]), .preset(1'b0), .en(en), .reset(rst));  // open: Qn
  assign out[5] = and_3_out ? dbg[5] : 1'bz;  // Controlled_Buffer controlled_buffer_3
  and and_3 (and_3_out, r, en);
  Multiplexer #(.enable("false")) multiplexer_4 (.in0(in[4]), .in1(dbg[4]), .out(multiplexer_4_out), .sel(nand_4_out));
  nand nand_4 (nand_4_out, w, en);
  D_Flip_Flop d_ff_4 (.clk(clk), .D(multiplexer_4_out), .Q(dbg[4]), .preset(1'b0), .en(en), .reset(rst));  // open: Qn
  assign out[4] = and_4_out ? dbg[4] : 1'bz;  // Controlled_Buffer controlled_buffer_4
  and and_4 (and_4_out, r, en);
  Multiplexer #(.enable("false")) multiplexer_5 (.in0(in[3]), .in1(dbg[3]), .out(multiplexer_5_out), .sel(nand_5_out));
  nand nand_5 (nand_5_out, w, en);
  assign out[3] = and_5_out ? dbg[3] : 1'bz;  // Controlled_Buffer controlled_buffer_5
  D_Flip_Flop d_ff_5 (.clk(clk), .D(multiplexer_5_out), .Q(dbg[3]), .preset(1'b0), .en(en), .reset(rst));  // open: Qn
  and and_5 (and_5_out, r, en);
  Multiplexer #(.enable("false")) multiplexer_6 (.in0(in[2]), .in1(dbg[2]), .out(multiplexer_6_out), .sel(nand_6_out));
  nand nand_6 (nand_6_out, w, en);
  D_Flip_Flop d_ff_6 (.clk(clk), .D(multiplexer_6_out), .Q(dbg[2]), .preset(1'b0), .en(en), .reset(rst));  // open: Qn
  assign out[2] = and_6_out ? dbg[2] : 1'bz;  // Controlled_Buffer controlled_buffer_6
  and and_6 (and_6_out, r, en);
  Multiplexer #(.enable("false")) multiplexer_7 (.in0(in[1]), .in1(dbg[1]), .out(multiplexer_7_out), .sel(nand_7_out));
  nand nand_7 (nand_7_out, w, en);
  D_Flip_Flop d_ff_7 (.clk(clk), .D(multiplexer_7_out), .Q(dbg[1]), .preset(1'b0), .en(en), .reset(rst));  // open: Qn
  and and_7 (and_7_out, r, en);
  Multiplexer #(.enable("false")) multiplexer_8 (.in0(in[0]), .in1(dbg[0]), .out(multiplexer_8_out), .sel(nand_8_out));
  assign out[1] = and_7_out ? dbg[1] : 1'bz;  // Controlled_Buffer controlled_buffer_7
  nand nand_8 (nand_8_out, w, en);
  D_Flip_Flop d_ff_8 (.clk(clk), .D(multiplexer_8_out), .Q(dbg[0]), .preset(1'b0), .en(en), .reset(rst));  // open: Qn
  assign out[0] = and_8_out ? dbg[0] : 1'bz;  // Controlled_Buffer controlled_buffer_8
  and and_8 (and_8_out, r, en);
endmodule

module ALU_2 (
  input  [7:0] a,
  input  [7:0] b,
  input  op2,
  input  op1,
  input  op0,
  input  cin,
  output [7:0] out,
  output overflow,
  output carry,
  output sign,
  output zero
);

  wire addsub8_1_carry, addsub8_1_out0, addsub8_1_out1, addsub8_1_out2, addsub8_1_out3, addsub8_1_out4,
       addsub8_1_out5, addsub8_1_out6, addsub8_1_out7, addsub8_1_overflow, ander8_1_out0, ander8_1_out1,
       ander8_1_out2, ander8_1_out3, ander8_1_out4, ander8_1_out5, ander8_1_out6, ander8_1_out7,
       leftshifter8_1_cout, leftshifter8_1_out0, leftshifter8_1_out1, leftshifter8_1_out2,
       leftshifter8_1_out3, leftshifter8_1_out4, leftshifter8_1_out6, leftshifter8_1_out6_2,
       leftshifter8_1_out7, nor_2_out, or_1_out, orer8_1_out0, orer8_1_out1, orer8_1_out2, orer8_1_out3,
       orer8_1_out4, orer8_1_out5, orer8_1_out6, orer8_1_out7, rightshifter8_1_cout, rightshifter8_1_out0,
       rightshifter8_1_out1, rightshifter8_1_out2, rightshifter8_1_out3, rightshifter8_1_out4,
       rightshifter8_1_out6, rightshifter8_1_out6_2, rightshifter8_1_out7, xorer8_1_out0, xorer8_1_out1,
       xorer8_1_out2, xorer8_1_out3, xorer8_1_out4, xorer8_1_out5, xorer8_1_out6, xorer8_1_out7;
  wire [7:0] decoder_1_out0;

  Ander8 ander8_1 (
    .a0(a[0]), .b0(b[0]), .a1(a[1]), .b1(b[1]), .a2(a[2]), .b2(b[2]), .a3(a[3]), .b3(b[3]), .a4(a[4]),
    .b4(b[4]), .a5(a[5]), .b5(b[5]), .a6(a[6]), .b6(b[6]), .a7(a[7]), .b7(b[7]), .out0(ander8_1_out0),
    .out1(ander8_1_out1), .out2(ander8_1_out2), .out3(ander8_1_out3), .out4(ander8_1_out4),
    .out5(ander8_1_out5), .out6(ander8_1_out6), .out7(ander8_1_out7));
  Orer8 orer8_1 (
    .a0(a[0]), .b0(b[0]), .a1(a[1]), .b1(b[1]), .a2(a[2]), .b2(b[2]), .a3(a[3]), .b3(b[3]), .a4(a[4]),
    .b4(b[4]), .a5(a[5]), .b5(b[5]), .a6(a[6]), .b6(b[6]), .a7(a[7]), .b7(b[7]), .out0(orer8_1_out0),
    .out1(orer8_1_out1), .out2(orer8_1_out2), .out3(orer8_1_out3), .out4(orer8_1_out4), .out5(orer8_1_out5),
    .out6(orer8_1_out6), .out7(orer8_1_out7));
  Xorer8 xorer8_1 (
    .a0(a[0]), .b0(b[0]), .a1(a[1]), .b1(b[1]), .a2(a[2]), .b2(b[2]), .a3(a[3]), .b3(b[3]), .a4(a[4]),
    .b4(b[4]), .a5(a[5]), .b5(b[5]), .a6(a[6]), .b6(b[6]), .a7(a[7]), .b7(b[7]), .out0(xorer8_1_out0),
    .out1(xorer8_1_out1), .out2(xorer8_1_out2), .out3(xorer8_1_out3), .out4(xorer8_1_out4),
    .out5(xorer8_1_out5), .out6(xorer8_1_out6), .out7(xorer8_1_out7));
  AddSub8 addsub8_1 (
    .cin(cin), .a0(a[0]), .b0(b[0]), .a1(a[1]), .b1(b[1]), .a2(a[2]), .b2(b[2]), .a3(a[3]), .b3(b[3]),
    .a4(a[4]), .b4(b[4]), .a5(a[5]), .b5(b[5]), .a6(a[6]), .b6(b[6]), .a7(a[7]), .b7(b[7]),
    .out0(addsub8_1_out0), .out1(addsub8_1_out1), .out2(addsub8_1_out2), .out3(addsub8_1_out3),
    .out4(addsub8_1_out4), .out5(addsub8_1_out5), .out6(addsub8_1_out6), .out7(addsub8_1_out7),
    .carry(addsub8_1_carry), .sub(decoder_1_out0[5]), .overflow(addsub8_1_overflow));
  LeftShifter8 leftshifter8_1 (
    .cin(cin), .in0(b[0]), .in1(b[1]), .in2(b[2]), .in3(b[3]), .in4(b[4]), .in5(b[5]), .in6(b[6]),
    .in7(b[7]), .out0(leftshifter8_1_out0), .out1(leftshifter8_1_out1), .out2(leftshifter8_1_out2),
    .out3(leftshifter8_1_out3), .out4(leftshifter8_1_out4), .out6(leftshifter8_1_out6),
    .out6_2(leftshifter8_1_out6_2), .out7(leftshifter8_1_out7), .cout(leftshifter8_1_cout));
  RightShifter8 rightshifter8_1 (
    .in0(b[0]), .in1(b[1]), .in2(b[2]), .in3(b[3]), .in4(b[4]), .in5(b[5]), .in6(b[6]), .in7(b[7]),
    .cin(cin), .cout(rightshifter8_1_cout), .out0(rightshifter8_1_out0), .out1(rightshifter8_1_out1),
    .out2(rightshifter8_1_out2), .out3(rightshifter8_1_out3), .out4(rightshifter8_1_out4),
    .out6(rightshifter8_1_out6), .out6_2(rightshifter8_1_out6_2), .out7(rightshifter8_1_out7));
  Decoder #(.select(3), .enable("false")) decoder_1 (
    .out0(decoder_1_out0[0]), .out1(decoder_1_out0[1]), .out2(decoder_1_out0[2]), .out3(decoder_1_out0[3]),
    .out4(decoder_1_out0[4]), .out5(decoder_1_out0[5]), .out6(decoder_1_out0[6]), .out7(decoder_1_out0[7]),
    .sel({op2, op1, op0}));
  Enabler8 enabler8_1 (
    .in0(b[0]), .in1(b[1]), .in2(b[2]), .in3(b[3]), .in4(b[4]), .in5(b[5]), .in6(b[6]), .in7(b[7]),
    .enable(decoder_1_out0[0]), .out0(out[0]), .out1(out[1]), .out2(out[2]), .out3(out[3]), .out4(out[4]),
    .out6(out[5]), .out6_2(out[6]), .out7(out[7]));
  Enabler8 enabler8_2 (
    .in0(ander8_1_out0), .in1(ander8_1_out1), .in2(ander8_1_out2), .in3(ander8_1_out3), .in4(ander8_1_out4),
    .in5(ander8_1_out5), .in6(ander8_1_out6), .in7(ander8_1_out7), .enable(decoder_1_out0[1]), .out0(out[0]),
    .out1(out[1]), .out2(out[2]), .out3(out[3]), .out4(out[4]), .out6(out[5]), .out6_2(out[6]), .out7(out[7]));
  Enabler8 enabler8_3 (
    .in0(orer8_1_out0), .in1(orer8_1_out1), .in2(orer8_1_out2), .in3(orer8_1_out3), .in4(orer8_1_out4),
    .in5(orer8_1_out5), .in6(orer8_1_out6), .in7(orer8_1_out7), .enable(decoder_1_out0[2]), .out0(out[0]),
    .out1(out[1]), .out2(out[2]), .out3(out[3]), .out4(out[4]), .out6(out[5]), .out6_2(out[6]), .out7(out[7]));
  Enabler8 enabler8_4 (
    .in0(xorer8_1_out0), .in1(xorer8_1_out1), .in2(xorer8_1_out2), .in3(xorer8_1_out3), .in4(xorer8_1_out4),
    .in5(xorer8_1_out5), .in6(xorer8_1_out6), .in7(xorer8_1_out7), .enable(decoder_1_out0[3]), .out0(out[0]),
    .out1(out[1]), .out2(out[2]), .out3(out[3]), .out4(out[4]), .out6(out[5]), .out6_2(out[6]), .out7(out[7]));
  or or_1 (or_1_out, decoder_1_out0[4], decoder_1_out0[5]);
  Enabler8 enabler8_5 (
    .in0(addsub8_1_out0), .in1(addsub8_1_out1), .in2(addsub8_1_out2), .in3(addsub8_1_out3),
    .in4(addsub8_1_out4), .in5(addsub8_1_out5), .in6(addsub8_1_out6), .in7(addsub8_1_out7),
    .enable(or_1_out), .out0(out[0]), .out1(out[1]), .out2(out[2]), .out3(out[3]), .out4(out[4]),
    .out6(out[5]), .out6_2(out[6]), .out7(out[7]));
  Enabler8 enabler8_6 (
    .in0(leftshifter8_1_out0), .in1(leftshifter8_1_out1), .in2(leftshifter8_1_out2),
    .in3(leftshifter8_1_out3), .in4(leftshifter8_1_out4), .in5(leftshifter8_1_out6),
    .in6(leftshifter8_1_out6_2), .in7(leftshifter8_1_out7), .enable(decoder_1_out0[6]), .out0(out[0]),
    .out1(out[1]), .out2(out[2]), .out3(out[3]), .out4(out[4]), .out6(out[5]), .out6_2(out[6]), .out7(out[7]));
  Enabler8 enabler8_7 (
    .in0(rightshifter8_1_out0), .in1(rightshifter8_1_out1), .in2(rightshifter8_1_out2),
    .in3(rightshifter8_1_out3), .in4(rightshifter8_1_out4), .in5(rightshifter8_1_out6),
    .in6(rightshifter8_1_out6_2), .in7(rightshifter8_1_out7), .enable(decoder_1_out0[7]), .out0(out[0]),
    .out1(out[1]), .out2(out[2]), .out3(out[3]), .out4(out[4]), .out6(out[5]), .out6_2(out[6]), .out7(out[7]));
  nor nor_1 (zero, out[7], out[6], out[5], out[4], out[3], out[2], out[1], out[0]);
  Multiplexer #(.enable("false")) multiplexer_1 (.in0(1'b0), .in1(addsub8_1_overflow), .out(overflow), .sel(or_1_out));
  nor nor_2 (nor_2_out, or_1_out, decoder_1_out0[6], decoder_1_out0[7]);
  assign carry = nor_2_out ? 1'b0 : 1'bz;  // Controlled_Buffer controlled_buffer_1
  assign carry = or_1_out ? addsub8_1_carry : 1'bz;  // Controlled_Buffer controlled_buffer_2
  assign carry = decoder_1_out0[6] ? leftshifter8_1_cout : 1'bz;  // Controlled_Buffer controlled_buffer_3
  assign carry = decoder_1_out0[7] ? rightshifter8_1_cout : 1'bz;  // Controlled_Buffer controlled_buffer_4

  assign sign = out[7];
endmodule

module Enabler8 (
  input  enable,
  input  in0,
  input  in1,
  input  in2,
  input  in3,
  input  in4,
  input  in5,
  input  in6,
  input  in7,
  output out0,
  output out1,
  output out2,
  output out3,
  output out4,
  output out6,
  output out6_2,
  output out7
);

  assign out0 = enable ? in0 : 1'bz;  // Controlled_Buffer controlled_buffer_1
  assign out1 = enable ? in1 : 1'bz;  // Controlled_Buffer controlled_buffer_2
  assign out2 = enable ? in2 : 1'bz;  // Controlled_Buffer controlled_buffer_3
  assign out3 = enable ? in3 : 1'bz;  // Controlled_Buffer controlled_buffer_4
  assign out4 = enable ? in4 : 1'bz;  // Controlled_Buffer controlled_buffer_5
  assign out6 = enable ? in5 : 1'bz;  // Controlled_Buffer controlled_buffer_6
  assign out6_2 = enable ? in6 : 1'bz;  // Controlled_Buffer controlled_buffer_7
  assign out7 = enable ? in7 : 1'bz;  // Controlled_Buffer controlled_buffer_8
endmodule

module LeftShifter8 (
  input  cin,
  input  in0,
  input  in1,
  input  in2,
  input  in3,
  input  in4,
  input  in5,
  input  in6,
  input  in7,
  output out0,
  output out1,
  output out2,
  output out3,
  output out4,
  output out6,
  output out6_2,
  output out7,
  output cout
);


  assign cout = in7;
  assign out0 = cin;
  assign out1 = in0;
  assign out2 = in1;
  assign out3 = in2;
  assign out4 = in3;
  assign out6 = in4;
  assign out6_2 = in5;
  assign out7 = in6;
endmodule

module RightShifter8 (
  input  in0,
  input  in1,
  input  in2,
  input  in3,
  input  in4,
  input  in5,
  input  in6,
  input  in7,
  input  cin,
  output cout,
  output out0,
  output out1,
  output out2,
  output out3,
  output out4,
  output out6,
  output out6_2,
  output out7
);


  assign cout = in0;
  assign out0 = in1;
  assign out1 = in2;
  assign out2 = in3;
  assign out3 = in4;
  assign out4 = in5;
  assign out6 = in6;
  assign out6_2 = in7;
  assign out7 = cin;
endmodule

module Notter8 (
  input  in0,
  input  in1,
  input  in2,
  input  in3,
  input  in4,
  input  in5,
  input  in6,
  input  in7,
  output out0,
  output out1,
  output out2,
  output out3,
  output out4,
  output out6,
  output out6_2,
  output out7
);

  not not_1 (out0, in0);
  not not_2 (out1, in1);
  not not_3 (out2, in2);
  not not_4 (out3, in3);
  not not_5 (out4, in4);
  not not_6 (out6, in5);
  not not_7 (out6_2, in6);
  not not_8 (out7, in7);
endmodule

module Ander8 (
  input  a0,
  input  b0,
  input  a1,
  input  b1,
  input  a2,
  input  b2,
  input  a3,
  input  b3,
  input  a4,
  input  b4,
  input  a5,
  input  b5,
  input  a6,
  input  b6,
  input  a7,
  input  b7,
  output out0,
  output out1,
  output out2,
  output out3,
  output out4,
  output out5,
  output out6,
  output out7
);

  and and_1 (out0, a0, b0);
  and and_2 (out1, a1, b1);
  and and_3 (out2, a2, b2);
  and and_4 (out3, a3, b3);
  and and_5 (out4, a4, b4);
  and and_6 (out5, a5, b5);
  and and_7 (out6, a6, b6);
  and and_8 (out7, a7, b7);
endmodule

module Orer8 (
  input  a0,
  input  b0,
  input  a1,
  input  b1,
  input  a2,
  input  b2,
  input  a3,
  input  b3,
  input  a4,
  input  b4,
  input  a5,
  input  b5,
  input  a6,
  input  b6,
  input  a7,
  input  b7,
  output out0,
  output out1,
  output out2,
  output out3,
  output out4,
  output out5,
  output out6,
  output out7
);

  or or_1 (out0, a0, b0);
  or or_2 (out1, a1, b1);
  or or_3 (out2, a2, b2);
  or or_4 (out3, a3, b3);
  or or_5 (out4, a4, b4);
  or or_6 (out5, a5, b5);
  or or_7 (out6, a6, b6);
  or or_8 (out7, a7, b7);
endmodule

module Xorer8 (
  input  a0,
  input  b0,
  input  a1,
  input  b1,
  input  a2,
  input  b2,
  input  a3,
  input  b3,
  input  a4,
  input  b4,
  input  a5,
  input  b5,
  input  a6,
  input  b6,
  input  a7,
  input  b7,
  output out0,
  output out1,
  output out2,
  output out3,
  output out4,
  output out5,
  output out6,
  output out7
);

  xor xor_1 (out0, a0, b0);
  xor xor_2 (out1, a1, b1);
  xor xor_3 (out2, a2, b2);
  xor xor_4 (out3, a3, b3);
  xor xor_5 (out4, a4, b4);
  xor xor_6 (out5, a5, b5);
  xor xor_7 (out6, a6, b6);
  xor xor_8 (out7, a7, b7);
endmodule

module FullAdder (
  input  a,
  input  b,
  input  cin,
  output sum,
  output cout
);

  wire and_1_out, and_2_out, xor_1_out;

  xor xor_1 (xor_1_out, a, b);
  xor xor_2 (sum, xor_1_out, cin);
  and and_1 (and_1_out, xor_1_out, cin);
  and and_2 (and_2_out, a, b);
  or or_1 (cout, and_1_out, and_2_out);
endmodule

module Adder8 (
  input  cin,
  input  a0,
  input  b0,
  input  a1,
  input  b1,
  input  a2,
  input  b2,
  input  a3,
  input  b3,
  input  a4,
  input  b4,
  input  a5,
  input  b5,
  input  a6,
  input  b6,
  input  a7,
  input  b7,
  output out0,
  output out1,
  output out2,
  output out3,
  output out4,
  output out5,
  output out6,
  output out7,
  output ovcarry,
  output cout
);

  wire fulladder_1_cout, fulladder_2_cout, fulladder_3_cout, fulladder_4_cout, fulladder_5_cout,
       fulladder_6_cout;

  FullAdder fulladder_1 (.a(a0), .b(b0), .cin(cin), .sum(out0), .cout(fulladder_1_cout));
  FullAdder fulladder_2 (.a(a1), .b(b1), .cin(fulladder_1_cout), .sum(out1), .cout(fulladder_2_cout));
  FullAdder fulladder_3 (.a(a2), .b(b2), .cin(fulladder_2_cout), .sum(out2), .cout(fulladder_3_cout));
  FullAdder fulladder_4 (.a(a3), .b(b3), .cin(fulladder_3_cout), .sum(out3), .cout(fulladder_4_cout));
  FullAdder fulladder_5 (.a(a4), .b(b4), .cin(fulladder_4_cout), .sum(out4), .cout(fulladder_5_cout));
  FullAdder fulladder_6 (.a(a5), .b(b5), .cin(fulladder_5_cout), .sum(out5), .cout(fulladder_6_cout));
  FullAdder fulladder_7 (.a(a6), .b(b6), .cin(fulladder_6_cout), .sum(out6), .cout(ovcarry));
  FullAdder fulladder_8 (.a(a7), .b(b7), .cin(ovcarry), .sum(out7), .cout(cout));
endmodule

module AddSub8 (
  input  sub,
  input  a0,
  input  b0,
  input  a1,
  input  b1,
  input  a2,
  input  b2,
  input  a3,
  input  b3,
  input  a4,
  input  b4,
  input  a5,
  input  b5,
  input  a6,
  input  b6,
  input  a7,
  input  b7,
  input  cin,
  output carry,
  output overflow,
  output out7,
  output out6,
  output out5,
  output out4,
  output out3,
  output out2,
  output out1,
  output out0
);

  wire adder8_1_cout, adder8_1_ovcarry, xor_3_out, xor_4_out, xor_5_out, xor_6_out, xor_7_out, xor_8_out,
       xor_9_out, xor_10_out, xor_11_out;

  xor xor_1 (carry, sub, adder8_1_cout);
  xor xor_2 (overflow, adder8_1_ovcarry, adder8_1_cout);
  xor xor_3 (xor_3_out, sub, b0);
  xor xor_4 (xor_4_out, sub, b1);
  xor xor_5 (xor_5_out, sub, b2);
  xor xor_6 (xor_6_out, sub, b3);
  xor xor_7 (xor_7_out, sub, b4);
  xor xor_8 (xor_8_out, sub, b5);
  xor xor_9 (xor_9_out, sub, b6);
  xor xor_10 (xor_10_out, sub, b7);
  Adder8 adder8_1 (
    .cin(xor_11_out), .a0(a0), .b0(xor_3_out), .a1(a1), .b1(xor_4_out), .a2(a2), .b2(xor_5_out), .a3(a3),
    .b3(xor_6_out), .a4(a4), .b4(xor_7_out), .a5(a5), .b5(xor_8_out), .a6(a6), .b6(xor_9_out), .a7(a7),
    .b7(xor_10_out), .out0(out0), .out1(out1), .out2(out2), .out3(out3), .out4(out4), .out5(out5),
    .out6(out6), .out7(out7), .ovcarry(adder8_1_ovcarry), .cout(adder8_1_cout));
  xor xor_11 (xor_11_out, sub, cin);
endmodule

module Inc8 (
  input  cin,
  input  [7:0] in,
  input  add_sub,
  output [7:0] out,
  output cout
);

  wire inc4_1_cout;

  Inc4 inc4_1 (
    .cin(cin), .add_sub(add_sub), .out0(out[0]), .in0(in[0]), .out1(out[1]), .in1(in[1]), .out2(out[2]),
    .in2(in[2]), .out3(out[3]), .in3(in[3]), .cout(inc4_1_cout));
  Inc4 inc4_2 (
    .cin(inc4_1_cout), .add_sub(add_sub), .out0(out[4]), .in0(in[4]), .out1(out[5]), .in1(in[5]),
    .out2(out[6]), .in2(in[6]), .out3(out[7]), .in3(in[7]), .cout(cout));
endmodule

module Inc4 (
  input  cin,
  input  in0,
  input  in1,
  input  in2,
  input  in3,
  input  add_sub,
  output out0,
  output out1,
  output out2,
  output out3,
  output cout
);

  wire and_1_out, and_2_out, and_3_out, and_4_out, and_5_out, and_6_out, and_7_out, and_8_out, or_1_out,
       or_2_out, or_3_out;

  xor xor_1 (out0, cin, in0);
  and and_1 (and_1_out, cin, in0, ~add_sub);  // AND_Gate
  and and_2 (and_2_out, cin, ~in0, add_sub);  // AND_Gate
  xor xor_2 (out1, or_1_out, in1);
  and and_3 (and_3_out, or_1_out, in1, ~add_sub);  // AND_Gate
  and and_4 (and_4_out, or_1_out, ~in1, add_sub);  // AND_Gate
  xor xor_3 (out2, or_2_out, in2);
  and and_5 (and_5_out, or_2_out, in2, ~add_sub);  // AND_Gate
  and and_6 (and_6_out, or_2_out, ~in2, add_sub);  // AND_Gate
  xor xor_4 (out3, or_3_out, in3);
  and and_7 (and_7_out, or_3_out, in3, ~add_sub);  // AND_Gate
  and and_8 (and_8_out, or_3_out, ~in3, add_sub);  // AND_Gate
  or or_1 (or_1_out, and_2_out, and_1_out);
  or or_2 (or_2_out, and_4_out, and_3_out);
  or or_3 (or_3_out, and_6_out, and_5_out);
  or or_4 (cout, and_8_out, and_7_out);
endmodule

module BranchChecker (
  input  zero,
  input  sign,
  input  carry,
  input  overflow,
  input  op2,
  input  op1,
  input  op0,
  output result
);

  wire and_1_out, and_2_out, and_3_out, and_4_out, and_5_out, and_6_out, and_7_out, decoder_1_out0,
       decoder_1_out1, decoder_1_out2, decoder_1_out3, decoder_1_out4, decoder_1_out5, decoder_1_out6,
       decoder_1_out7, or_1_out, or_2_out, xor_1_out;

  Decoder #(.select(3), .enable("false")) decoder_1 (
    .out0(decoder_1_out0), .out1(decoder_1_out1), .out2(decoder_1_out2), .out3(decoder_1_out3),
    .out4(decoder_1_out4), .out5(decoder_1_out5), .out6(decoder_1_out6), .out7(decoder_1_out7),
    .sel({op2, op1, op0}));
  or or_1 (or_1_out, zero, xor_1_out);
  xor xor_1 (xor_1_out, overflow, sign);
  or or_2 (or_2_out, carry, zero);
  and and_1 (and_1_out, decoder_1_out1, zero);
  and and_2 (and_2_out, decoder_1_out2, sign);
  and and_3 (and_3_out, decoder_1_out3, overflow);
  and and_4 (and_4_out, decoder_1_out4, carry);
  and and_5 (and_5_out, decoder_1_out5, or_2_out);
  and and_6 (and_6_out, decoder_1_out6, xor_1_out);
  and and_7 (and_7_out, decoder_1_out7, or_1_out);
  or or_3 (result, and_7_out, and_6_out, and_5_out, and_4_out, and_3_out, and_2_out, and_1_out, decoder_1_out0);
endmodule
